# Fritzing sketch aquaMonitor (saved by Fritzing 0.9.2b)
breadboards: 1

parts:
  Composant1 = Arduino GSM Shield
  U1 = POT [part_number=P1 package=pot_alpha_rv16af-20]
  U2 = LCD-16X2 [part_number=LCD package=lcd-16x2_noholes]
  Composant3 = Real Time Clock Module - DS1307 RTC Breakout Board [part_number=RTC]
  U3 = TEMPERATURE-SENSOR [part_number=DS18B20 package=to-92]
  R1 = PHOTOCELL [part_number=LDR package=photocell]
  IR1 = TSOP312.., 314.. [part_number=IR package=THT]
  R2 = Resistor [tolerance=±5% resistance=10k package="0603 [SMD]"]
  R3 = Resistor [tolerance=±5% resistance=4.7k package="2010 [SMD]"]
  Composant4 = Arduino Uno (Rev3) - ICSP  # not connected
  S1 = Floater Switch

nets:
  N1: Composant1.A5/SCL, Composant3.SCL
  N2: Composant1.A4/SDA, Composant3.SDA
  N3: Composant1.MISO/D12, U2.DB7
  N4: Composant1.MOSI/PWM_D11, U2.DB6
  N5: Composant1.SS/PWM_D10, U2.DB5
  N6: Composant1.PWM_D9, U2.DB4
  N7: Composant1.D8, U2.E
  5V: Composant1.5V, U2.VDD, Composant3.5V, U3.ADJ, R1.P$2, IR1.Data, R3.Pin_0
  GND: Composant1.AGND, U1.A, U2.VSS, U2.R_W, Composant3.GND, U3.GND, IR1.Vs, R2.Pin_1, S1.leg0
  N8: Composant1.PWM_D4, S1.leg1
  N9: Composant1.PWM_D5, IR1.GND
  N10: Composant1.PWM_D6, U3.VCC, R3.Pin_1
  N11: Composant1.RST_MDM/D7, U2.RS
  N12: Composant1.A0, R1.P$1, R2.Pin_0
  N13: U1.S, U2.VO

custom parts:
  Floater Switch: Water level switch
